// Digital circuit d-latch-clr.dig as structural Verilog
module d_latch_clr (
  input  CLK,
  input  CLR,
  input  D,
  output Q,
  output notQ
);

  wire and_1_out, or_1_out;

  or or_1 (or_1_out, CLK, CLR);
  and and_1 (and_1_out, D, ~CLR);  // And
  d_latch d_latch_1 (.CLK(or_1_out), .D(and_1_out), .Q(Q), .notQ(notQ));
endmodule
