// Digital circuit p05-sketch.dig as structural Verilog
module p05_sketch (
  input  [7:0] in_1,
  input  [1:0] PN,
  input  [31:0] in_4,
  input  clk,
  output [31:0] iw,
  output [2:0] inum
);

  wire [6:0] xnor_1_out;
  wire [31:0] is_pal_d;

  assign xnor_1_out = ~(in_4[6:0] ^ 7'b1100111);  // XNOr xnor_1, 7 bits wide
  PriorityEncoder #(.Selector_Bits(3)) priorityencoder_1 (
    .in0(xnor_1_out[0]), .num(inum));  // open: in1, in2, in3, in4, in5, in6, in7, any
  ROM #(.AddrBits(8), .Bits(32)) is_pal (.A(in_1), .sel(1'b1), .D(is_pal_d));
  // Probe on is_pal_d
  Multiplexer #(.Bits(32), .Selector_Bits(2)) multiplexer_1 (
    .sel(PN), .in_0(is_pal_d), .out(iw));  // open: in_1, in_2, in_3
  // Pins of 1 and 32 bits meet at in_4
  // Pins of 1 and 7 bits meet at xnor_1_out

  // Notes on the sheet:
  //   contents of is_pal (hex, n*v repeats v):
  //   13,13,13,c5c663,100513,3c0006f,b502b3,28283,c50333,30303,628663
  //   ,513,200006f,ff810113,113023,158593,fff60613,fc9ff0ef,13083,810113
  //   ,8067,c0001073
  //   Instr Mem sketch
endmodule
